# Fritzing sketch quickdraw_circuit (saved by Fritzing 0.9.3b)
breadboards: 3
stripboards: 1

parts:
  Raspberry_Pi_1 = Raspberry Pi 3 [part_number=RPI-3-V1.2]
  IC1 = MCP3008 8-channel 10-bit ADC [part_number=MCP3008]
  J4 = Screw terminal - 2 pins [package=THT]
  J5 = Screw terminal - 2 pins [package=THT]
  J6 = Piezo Speaker
  U1 = attiny85 [package=dip]
  R9 = Resistor [tolerance=±5% resistance=1M package=THT]
  J7 = Screw terminal - 2 pins [package=THT]
  J8 = Screw terminal - 2 pins [package=THT]
  J9 = Screw terminal - 2 pins [package=THT]
  J11 = Screw terminal - 2 pins [package=THT]
  DOTSTAR1 = DotStar Strip -- Black (60/m) [part_number=2239]
  PART1 = Tiny AVR Programmer [part_number=PGM-11801]  # not connected
  S1 = Toggle Switch [package=THT]
  S2 = Toggle Switch [package=THT]
  J12 = Screw terminal - 2 pins [package=THT]
  C1 = Capacitor [package=cap-pth-small2]
  U2 = attiny85 [package=dip]
  J13 = Camdenboss CTB0158-2 [part_number=CTB0158-2 package=THT]  # not connected
  DOTSTAR2 = DotStar Strip -- Black (60/m) [part_number=2239]  # not connected
  J14 = Camdenboss CTB0158-2 [part_number=CTB0158-2 package=THT]
  J15 = Camdenboss CTB0158-2 [part_number=CTB0158-2 package=THT]
  J16 = Camdenboss CTB0158-2 [part_number=CTB0158-2 package=THT]
  J18 = Camdenboss CTB0158-2 [part_number=CTB0158-2 package=THT]
  J19 = Piezo Speaker
  R11 = Resistor [tolerance=±5% resistance=220 package=THT]
  R12 = Resistor [tolerance=±5% resistance=220 package="2512 [SMD]"]  # not connected
  R13 = Resistor [tolerance=±5% resistance=220 package=THT]
  R14 = Resistor Mini [tolerance=±5% resistance=220 package=THT]

nets:
  N1: Raspberry_Pi_1.3V3, Raspberry_Pi_1.GPIO10, IC1.no_name_yet#11
  N2: Raspberry_Pi_1.GPIO9, IC1.no_name_yet#12
  N3: Raspberry_Pi_1.GPIO11, IC1.no_name_yet#13
  N4: Raspberry_Pi_1.GPIO8, IC1.no_name_yet#10
  N5: Raspberry_Pi_1.GND, IC1.no_name_yet#9, IC1.no_name_yet#14
  N6: Raspberry_Pi_1.5V, IC1.no_name_yet#15, IC1.no_name_yet#16, S1.L1
  N7: IC1.no_name_yet#1, J5.pin1
  N8: IC1.no_name_yet#2, J5.pin2
  N9: IC1.no_name_yet#3, J7.pin1
  N10: IC1.no_name_yet#4, J7.pin2
  N11: IC1.no_name_yet#5, J8.pin1
  N12: IC1.no_name_yet#6, J8.pin2
  N13: IC1.no_name_yet#7, J9.pin1, S2.COM
  N14: IC1.no_name_yet#8, J9.pin2
  N15: J4.pin1, U1.Pin_1
  N16: J4.pin2, U1.Pin_2, DOTSTAR1.DI
  N17: J6.pin1, U1.Pin_4, R9.Pin_0, J11.pin2, DOTSTAR1.GND, J12.pin2
  N18: J6.pin2, U1.Pin_7, R9.Pin_1, J12.pin1
  N19: U1.Pin_3, J11.pin1, DOTSTAR1.CI
  N20: S1.COM, S2.L1
  N21: C1.1, U2.Pin_7, J15.pin1, J16.pin1, J19.pin1, R14.Pin_1
  N22: C1.2, U2.Pin_8, J15.pin2
  N23: U2.Pin_2, J14.pin2
  N24: U2.Pin_3, J14.pin1
  N25: U2.Pin_4, J16.pin2, J19.pin2, R14.Pin_0
  N26: U2.Pin_5, J18.pin2
  N27: U2.Pin_6, J18.pin1
  N28: R11.Pin_0, R13.Pin_0
  N29: R11.Pin_1, R13.Pin_1

custom parts:
  DotStar Strip -- Black (60/m): NeopixelDotStar Strip, Black, 60 pixels per meter.
  Tiny AVR Programmer: The ATtiny45 and 85 are a couple of really cool little MCUs but did you know you can program them in Arduino? That’s right, now you can shrink your Arduino projects down to “tiny size” by moving your code straight over to these small but capable ICs. The standard method for programming the ATtiny ICs involves a breadboard, lots of jumper wires and a hardware programmer, but David Mellis over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
  Resistor Mini: A generic resistor (0.25W)
